// Logisim project 2 BIT COMPARATOR.circ as structural Verilog: 1 circuit, main circuit main
module main (
  input  A0,
  input  A1,
  input  B0,
  input  B1,
  output A___B,
  output A___B_2,
  output A___B_3
);

  wire and_1_out, and_2_out, and_3_out, and_4_out, and_5_out, and_6_out, not_1_out, not_2_out, not_3_out,
       not_4_out, xnor_1_out, xnor_2_out;

  not not_1 (not_1_out, A0);
  not not_2 (not_2_out, A1);
  not not_3 (not_3_out, B0);
  not not_4 (not_4_out, B1);
  and and_1 (and_1_out, not_1_out, B0);
  and and_2 (and_2_out, not_1_out, not_2_out, B1);
  and and_3 (and_3_out, not_2_out, not_3_out, B1);
  and and_4 (and_4_out, A0, not_3_out);
  and and_5 (and_5_out, A1, not_3_out, not_4_out);
  and and_6 (and_6_out, A0, A1, not_4_out);
  xnor xnor_1 (xnor_1_out, not_1_out, not_3_out);
  xnor xnor_2 (xnor_2_out, A1, B1);
  or or_1 (A___B, and_1_out, and_2_out, and_3_out);
  and and_7 (A___B_2, xnor_1_out, xnor_2_out);
  or or_2 (A___B_3, and_4_out, and_5_out, and_6_out);
endmodule
